# Fritzing sketch rgbLED_schematic (saved by Fritzing 0.9.3b)
breadboards: 1

parts:
  Part1 = Arduino Mega 2560 (Rev3)
  R1 = Resistor [tolerance=±5% resistance=220 package=THT]
  R2 = Resistor [tolerance=±5% resistance=220 package=THT]
  R3 = Resistor [tolerance=±5% resistance=220 package=THT]
  LED2 = RGB LED - (4 legs) [package="5 mm [THT]"]

nets:
  N1: Part1.D3_PWM, R3.Pin_0
  N2: Part1.D5_PWM, R2.Pin_0
  N3: Part1.D6_PWM, R1.Pin_0
  N4: R1.Pin_1, R2.Pin_1, R3.Pin_1, LED2.common_anode
